// Logisim project NAND Cir.circ as structural Verilog: 1 circuit, main circuit main
module main (
  input  in_1,
  input  in_2,
  input  in_3,
  output out_4
);

  wire A_prime_B_prime_C_out, A_prime_BC_out, AB_prime_C_out, AB_prime_C_prime_out, ABC_out, not_1_out,
       not_2_out, not_3_out;

  not not_1 (not_1_out, in_1);
  not not_2 (not_2_out, in_2);
  not not_3 (not_3_out, in_3);
  nand A_prime_BC (A_prime_BC_out, not_1_out, in_2, in_3);
  nand AB_prime_C_prime (AB_prime_C_prime_out, in_1, not_2_out, not_3_out);
  nand ABC (ABC_out, in_1, in_2, in_3);
  nand AB_prime_C (AB_prime_C_out, in_1, not_2_out, in_3);
  nand A_prime_B_prime_C (A_prime_B_prime_C_out, not_1_out, not_2_out, in_3);
  nand f (out_4, ABC_out, A_prime_BC_out, AB_prime_C_out, AB_prime_C_prime_out, A_prime_B_prime_C_out);
endmodule
